# Fritzing sketch Haruspex (saved by Fritzing 0.9.6b)
breadboards: 1

parts:
  Mod1 = Heltec WiFi LoRa 32 V2 [part_number=HTIT-WB32LA]

nets:
  N1: Mod1.pin_16, Mod1.pin_17
  N2: Mod1.pin_21, Mod1.pin_22

// code stored in the sketch: main.cpp.ino
#include <Arduino.h>

void setup() {

}

void loop() {

}
